// Logisim project Datapath.circ as structural Verilog: 6 circuits, main circuit main
module main (
  input  clear,
  output [7:0] Display,
  output out_3,
  output out_4,
  output [1:0] out_5,
  output out_6,
  output [1:0] out_7,
  output out_8,
  output [1:0] out_9,
  output out_10,
  output out_11,
  output [1:0] out_12,
  output out_13,
  output out_14,
  output out_15
);

  wire alu_8_bit_1_out_10, and_1_out, clock_1_out;
  wire [1:0] multiplexer_1_out;
  wire [3:0] rom_1_data;
  wire [4:0] shifter_1_out;
  wire [4:1] rom_1_data_2;
  wire [7:0] adder_1_out, adder_2_out, alu_8_bit_1_out_8, bit_extender_1_out, bit_extender_2_out,
       bit_extender_3_out, multiplexer_2_out, multiplexer_3_out, multiplexer_4_out, multiplexer_5_out,
       ram_1_data, register_1_q, register_file_1_data_1, register_file_1_data_2, register_file_1_out_9,
       register_file_1_out_10, shifter_2_out;

  Register register_1 (.D(multiplexer_4_out), .Q(register_1_q), .clk(clock_1_out), .clr(clear));  // open: en
  Clock clock_1 (.out(clock_1_out));
  Adder adder_1 (.a(register_1_q), .b(8'h1), .out(adder_1_out));  // open: cin, cout
  ROM rom_1 (.addr(register_1_q), .data({rom_1_data[2:0], rom_1_data_2, rom_1_data[3]}));  // open: sel
  assign bit_extender_1_out = {{5{1'b0}}, {rom_1_data_2[2:1], rom_1_data[3]}};  // Bit_Extender bit_extender_1
  Shifter #(.width(5)) shifter_1 (.in({rom_1_data_2, rom_1_data[3]}), .\dist (3'b000), .out(shifter_1_out));
  Multiplexer #(.select(2), .width(2), .enable("false")) multiplexer_1 (
    .in0(rom_1_data_2[4:3]), .in1(rom_1_data_2[2:1]), .in2(2'b11), .out(multiplexer_1_out), .sel(out_5));  // open: in3
  main_control_unit main_control_unit_1 (
    .in_1(rom_1_data), .out_2(out_5), .reg_wrt(out_6), .out_4(out_7), .b_invert(out_8), .ALU_op(out_9),
    .str__enbl(out_10), .out_8(out_11), .out_9(out_12), .beq(out_13), .jump(out_14), .disp(out_15));
  assign bit_extender_2_out = {{3{1'b0}}, shifter_1_out};  // Bit_Extender bit_extender_2
  register_file register_file_1 (
    .clock(clock_1_out), .write_data(multiplexer_5_out), .wrt_data(out_6), .data_1(register_file_1_data_1),
    .data_2(register_file_1_data_2), .in_5(multiplexer_1_out), .Read_reg_1(rom_1_data_2[4:3]),
    .in_6(rom_1_data_2[2:1]), .in_7(clear), .out_10(register_file_1_out_10), .out_9(register_file_1_out_9));
  Shifter shifter_2 (.in(bit_extender_1_out), .\dist (3'b000), .out(shifter_2_out));
  Multiplexer #(.select(2), .width(8), .enable("false")) multiplexer_2 (
    .in0(register_file_1_data_2), .in1(bit_extender_1_out), .in2(register_file_1_out_9),
    .out(multiplexer_2_out), .sel(out_7));  // open: in3
  Adder adder_2 (.a(adder_1_out), .b(shifter_2_out), .out(adder_2_out));  // open: cin, cout
  Multiplexer #(.width(8), .enable("false")) multiplexer_3 (
    .in0(adder_1_out), .in1(adder_2_out), .out(multiplexer_3_out), .sel(and_1_out));
  ALU_8_bit alu_8_bit_1 (
    .in_1(register_file_1_data_1), .B(multiplexer_2_out), .A_prime(1'b0), .B_prime(out_8),
    .out_8(alu_8_bit_1_out_8), .Overflow(out_4), .C_in(out_8), .ALU_op(out_9), .out_7(out_3),
    .out_10(alu_8_bit_1_out_10));
  and and_1 (and_1_out, out_13, out_3);
  assign bit_extender_3_out = {{7{1'b0}}, alu_8_bit_1_out_10};  // Bit_Extender bit_extender_3
  Multiplexer #(.width(8), .enable("false")) multiplexer_4 (
    .in0(multiplexer_3_out), .in1(bit_extender_2_out), .out(multiplexer_4_out), .sel(out_14));
  RAM #(.bus("separate")) ram_1 (
    .addr(alu_8_bit_1_out_8), .din(register_file_1_out_10), .data(ram_1_data), .str(out_10),
    .clk(clock_1_out), .ld(out_11), .clr(clear));  // open: sel
  Multiplexer #(.select(2), .width(8), .enable("false")) multiplexer_5 (
    .in0(alu_8_bit_1_out_8), .in1(ram_1_data), .in2(bit_extender_3_out), .in3(register_file_1_out_10),
    .out(multiplexer_5_out), .sel(out_12));
  Multiplexer #(.width(8), .enable("false")) multiplexer_6 (
    .in1(multiplexer_5_out), .out(Display), .sel(out_15));  // open: in0

  // Notes on the sheet:
  //                  reg slct to wrt data
  //   reg wrt
  //                 immediate load
  //          A invert
  //   B invert 
  //   ALU Op
  //   Store enbl
  //   load enable
  //   mem slct
  //   beq
  //   jump slct
  //   DISP cntrl
  //   contents of rom_1 (hex, n*v repeats v):
  //   a7 9c 2a 31 21 c0 1f e 73 1f 0 0 53 e0
endmodule

module register_file (
  input  clock,
  input  [7:0] write_data,
  input  wrt_data,
  input  [1:0] Read_reg_1,
  input  [1:0] in_5,
  input  [1:0] in_6,
  input  in_7,
  output [7:0] data_1,
  output [7:0] out_9,
  output [7:0] out_10,
  output [7:0] data_2
);

  wire and_1_out, and_2_out, and_3_out, and_4_out, decoder_1_out0, decoder_1_out1, decoder_1_out2,
       decoder_1_out3;
  wire [7:0] register_1_q, register_2_q, register_3_q;

  Decoder #(.select(2)) decoder_1 (
    .out0(decoder_1_out0), .out1(decoder_1_out1), .out2(decoder_1_out2), .out3(decoder_1_out3), .sel(in_5));  // open: en
  and and_1 (and_1_out, wrt_data, decoder_1_out0);
  and and_2 (and_2_out, wrt_data, decoder_1_out1);
  and and_3 (and_3_out, wrt_data, decoder_1_out2);
  and and_4 (and_4_out, wrt_data, decoder_1_out3);
  Register register_1 (.D(write_data), .en(and_1_out), .Q(register_1_q), .clk(clock), .clr(in_7));
  Register register_2 (.D(write_data), .en(and_2_out), .Q(register_2_q), .clk(clock), .clr(in_7));
  Register register_3 (.D(write_data), .en(and_3_out), .Q(register_3_q), .clk(clock), .clr(in_7));
  Register register_4 (.D(write_data), .en(and_4_out), .Q(out_10), .clk(clock), .clr(in_7));
  Multiplexer #(.select(2), .width(8)) multiplexer_1 (
    .in0(register_1_q), .in1(register_2_q), .in2(register_3_q), .in3(out_10), .out(data_1), .sel(Read_reg_1));  // open: en
  Multiplexer #(.select(2), .width(8)) multiplexer_2 (
    .in0(register_1_q), .in1(register_2_q), .in2(register_3_q), .in3(out_10), .out(data_2), .sel(in_6));  // open: en

  assign out_9 = {8{1'b0}};

  // Notes on the sheet:
  //   write register
  //   $T0
  //   $t1
  //   $t2
  //   $t3
  //   reset
  //   Read Reg 2
  //   zero reg
  //      t3 reg
endmodule

module ALU_1_bit (
  input  in_1,
  input  A,
  input  B,
  input  in_4,
  input  B_invert,
  input  [1:0] ALU_OP,
  output Output,
  output out_8
);

  wire adder_1_out, and_1_out, multiplexer_1_out, multiplexer_2_out, not_1_out, not_2_out, or_1_out,
       xor_1_out;

  Multiplexer #(.enable("false")) multiplexer_1 (.in0(A), .in1(not_1_out), .out(multiplexer_1_out), .sel(in_4));
  not not_1 (not_1_out, A);
  Multiplexer #(.enable("false")) multiplexer_2 (.in0(B), .in1(not_2_out), .out(multiplexer_2_out), .sel(B_invert));
  not not_2 (not_2_out, B);
  and and_1 (and_1_out, multiplexer_1_out, multiplexer_2_out);
  or or_1 (or_1_out, multiplexer_1_out, multiplexer_2_out);
  xor xor_1 (xor_1_out, multiplexer_1_out, multiplexer_2_out);
  Adder #(.width(1)) adder_1 (
    .a(multiplexer_2_out), .b(multiplexer_1_out), .out(adder_1_out), .cin(in_1), .cout(out_8));
  Multiplexer #(.select(2), .enable("false")) multiplexer_3 (
    .in0(and_1_out), .in1(or_1_out), .in2(xor_1_out), .in3(adder_1_out), .out(Output), .sel(ALU_OP));

  // Notes on the sheet:
  //   A invert
endmodule

module ALU_8_bit (
  input  [7:0] in_1,
  input  C_in,
  input  [7:0] B,
  input  A_prime,
  input  B_prime,
  input  [1:0] ALU_op,
  output out_7,
  output [7:0] out_8,
  output Overflow,
  output out_10
);

  wire alu_1_bit_1_out_8, alu_1_bit_2_out_8, alu_1_bit_3_out_8, alu_1_bit_4_out_8, alu_1_bit_5_out_8,
       alu_1_bit_6_out_8, alu_1_bit_7_out_8, alu_1_bit_8_out_8;

  ALU_1_bit alu_1_bit_1 (
    .A(in_1[0]), .B(B[0]), .Output(out_8[0]), .ALU_OP(ALU_op), .in_4(A_prime), .B_invert(B_prime),
    .in_1(C_in), .out_8(alu_1_bit_1_out_8));
  ALU_1_bit alu_1_bit_2 (
    .A(in_1[1]), .B(B[1]), .Output(out_8[1]), .ALU_OP(ALU_op), .in_4(A_prime), .B_invert(B_prime),
    .in_1(alu_1_bit_1_out_8), .out_8(alu_1_bit_2_out_8));
  ALU_1_bit alu_1_bit_3 (
    .A(in_1[2]), .B(B[2]), .Output(out_8[2]), .ALU_OP(ALU_op), .in_4(A_prime), .B_invert(B_prime),
    .in_1(alu_1_bit_2_out_8), .out_8(alu_1_bit_3_out_8));
  ALU_1_bit alu_1_bit_4 (
    .A(in_1[3]), .B(B[3]), .Output(out_8[3]), .ALU_OP(ALU_op), .in_4(A_prime), .B_invert(B_prime),
    .in_1(alu_1_bit_3_out_8), .out_8(alu_1_bit_4_out_8));
  ALU_1_bit alu_1_bit_5 (
    .A(in_1[4]), .B(B[4]), .Output(out_8[4]), .ALU_OP(ALU_op), .in_4(A_prime), .B_invert(B_prime),
    .in_1(alu_1_bit_4_out_8), .out_8(alu_1_bit_5_out_8));
  ALU_1_bit alu_1_bit_6 (
    .A(in_1[5]), .B(B[5]), .Output(out_8[5]), .ALU_OP(ALU_op), .in_4(A_prime), .B_invert(B_prime),
    .in_1(alu_1_bit_5_out_8), .out_8(alu_1_bit_6_out_8));
  ALU_1_bit alu_1_bit_7 (
    .A(in_1[6]), .B(B[6]), .Output(out_8[6]), .ALU_OP(ALU_op), .in_4(A_prime), .B_invert(B_prime),
    .in_1(alu_1_bit_6_out_8), .out_8(alu_1_bit_7_out_8));
  ALU_1_bit alu_1_bit_8 (
    .A(in_1[7]), .B(B[7]), .Output(out_8[7]), .ALU_OP(ALU_op), .in_4(A_prime), .B_invert(B_prime),
    .in_1(alu_1_bit_7_out_8), .out_8(alu_1_bit_8_out_8));
  xor xor_1 (Overflow, alu_1_bit_7_out_8, alu_1_bit_8_out_8);
  nor nor_1 (out_7, out_8[0], out_8[1], out_8[2], out_8[3], out_8[4], out_8[5], out_8[6], out_8[7]);

  assign out_10 = out_8[7];

  // Notes on the sheet:
  //   A
  //             output
  //             ZEROFLAG
  //                                                  negative detection 
endmodule

module main_control_unit (
  input  [3:0] in_1,
  output [1:0] out_2,
  output reg_wrt,
  output [1:0] out_4,
  output b_invert,
  output [1:0] ALU_op,
  output str__enbl,
  output out_8,
  output [1:0] out_9,
  output beq,
  output jump,
  output disp
);

  wire add_out, addi_out, not_1_out, not_2_out, not_3_out, not_4_out, slti_out, sub_out;

  not not_1 (not_1_out, in_1[1]);
  not not_2 (not_2_out, in_1[0]);
  not not_3 (not_3_out, in_1[2]);
  not not_4 (not_4_out, in_1[3]);
  and add (add_out, not_4_out, not_2_out, not_1_out, not_3_out);
  and sub (sub_out, in_1[3], not_2_out, not_1_out, not_3_out);
  and addi (addi_out, in_1[0], not_1_out, not_3_out);
  and lw (out_8, not_2_out, in_1[1], not_3_out);
  and sw (str__enbl, in_1[0], in_1[1], not_3_out);
  and u_beq (beq, not_2_out, not_1_out, in_1[2]);
  and slti (slti_out, in_1[0], not_1_out, in_1[2]);
  and u_disp (disp, in_1[0], in_1[1], in_1[2]);
  and u_jump (jump, not_2_out, in_1[1], in_1[2]);
  or or_1 (out_2[0], add_out, sub_out);
  or or_2 (out_2[1], out_8, str__enbl, slti_out);
  or or_3 (reg_wrt, add_out, addi_out, out_8, slti_out, sub_out);
  or or_4 (out_4[0], addi_out, out_8, str__enbl, slti_out);
  or or_5 (b_invert, beq, slti_out, sub_out);
  or or_6 (out_9[0], out_8, str__enbl, disp);
  or or_7 (out_9[1], slti_out, disp);

  assign ALU_op = 2'b11;
  assign out_4[1] = beq;

  // Notes on the sheet:
  //                                       reg slct to wrt data
  //                                imm load
  //                                lw enable
  //                        mem slct
endmodule

module BCD_to_7_segment (
  input  A,
  input  B,
  input  C,
  input  D,
  input  in_5,
  output out_6,
  output out_7,
  output out_8,
  output out_9,
  output out_10,
  output out_11,
  output out_12
);

  wire and_1_out, and_2_out, and_3_out, and_4_out, and_5_out, and_6_out, and_7_out, and_8_out, and_9_out,
       not_1_out, not_2_out, not_3_out, not_4_out, or_1_out, or_2_out, or_3_out, or_4_out, or_5_out,
       or_6_out, or_7_out;

  not not_1 (not_1_out, A);
  not not_2 (not_2_out, B);
  not not_3 (not_3_out, C);
  not not_4 (not_4_out, D);
  and and_1 (and_1_out, B, D);
  and and_2 (and_2_out, not_2_out, not_4_out);
  and and_3 (and_3_out, C, D);
  and and_4 (and_4_out, not_3_out, not_4_out);
  and and_5 (and_5_out, C, not_4_out);
  and and_6 (and_6_out, not_2_out, C);
  and and_7 (and_7_out, B, not_3_out);
  and and_8 (and_8_out, B, not_4_out);
  and and_9 (and_9_out, D, and_7_out);
  or or_1 (or_1_out, and_3_out, not_2_out, and_4_out);
  or or_2 (or_2_out, B, not_3_out, D);
  or or_3 (or_3_out, A, and_2_out, and_5_out, and_6_out, and_9_out);
  or or_4 (or_4_out, and_2_out, and_5_out);
  or or_5 (or_5_out, and_4_out, and_8_out, and_7_out, A);
  or or_6 (or_6_out, and_5_out, and_7_out, A, and_6_out);
  or or_7 (or_7_out, and_1_out, C, A, and_2_out);
  and and_10 (out_6, or_7_out, in_5);
  and and_11 (out_7, or_1_out, in_5);
  and and_12 (out_8, or_2_out, in_5);
  and and_13 (out_9, or_3_out, in_5);
  and and_14 (out_10, or_4_out, in_5);
  and and_15 (out_11, or_5_out, in_5);
  and and_16 (out_12, or_6_out, in_5);
  _7_Segment_Display u_7_segment_display_1 (
    .g(out_12), .f(out_11), .a(out_6), .b(out_7), .e(out_10), .d(out_9), .c(out_8));  // open: dp
endmodule
